// Logisim project NAND.circ as structural Verilog: 1 circuit, main circuit main
module main (
  input  A,
  input  B,
  input  A_2,
  input  A_3,
  input  B_2,
  input  A_4,
  input  B_3,
  output A_NAND_B,
  output NOT_A,
  output out_10,
  output out_11,
  output A_AND_B,
  output out_13,
  output A_OR_B
);

  wire nand_3_out, nand_4_out, nand_5_out, nand_6_out;

  nand nand_1 (A_NAND_B, A, B);
  nand nand_2 (out_10, A_2, A_2);
  nand nand_3 (nand_3_out, A_3, B_2);
  nand nand_4 (nand_4_out, A_3, B_2);
  nand nand_5 (nand_5_out, A_4, A_4);
  nand nand_6 (nand_6_out, B_3, B_3);
  not not_1 (NOT_A, A_2);
  nand nand_7 (out_11, nand_3_out, nand_4_out);
  nand nand_8 (out_13, nand_5_out, nand_6_out);
  and and_1 (A_AND_B, A_3, B_2);
  or or_1 (A_OR_B, A_4, B_3);
endmodule
