// Logisim project NOR.circ as structural Verilog: 1 circuit, main circuit main
module main (
  input  A,
  input  B,
  input  A_2,
  input  A_3,
  input  B_2,
  input  A_4,
  input  B_3,
  output A_NOR_B,
  output NOT_A,
  output out_10,
  output out_11,
  output A_AND_B,
  output out_13,
  output A_OR_B
);

  wire nor_3_out, nor_4_out, nor_5_out, nor_6_out;

  nor nor_1 (A_NOR_B, A, B);
  nor nor_2 (out_10, A_2, A_2);
  nor nor_3 (nor_3_out, A_3, A_3);
  nor nor_4 (nor_4_out, B_2, B_2);
  nor nor_5 (nor_5_out, A_4, B_3);
  nor nor_6 (nor_6_out, A_4, B_3);
  not not_1 (NOT_A, A_2);
  nor nor_7 (out_11, nor_3_out, nor_4_out);
  nor nor_8 (out_13, nor_5_out, nor_6_out);
  and and_1 (A_AND_B, A_3, B_2);
  or or_1 (A_OR_B, A_4, B_3);
endmodule
